# Fritzing sketch LCD2004_I2C (saved by Fritzing 0.9.2b)

parts:
  LCM1602_IIC2 = LCM1602 IIC [part_number="LCM1602 IIC" chip_label="LCM1602 IIC" package="DIP (Dual Inline) [THT]"]
  LCD3 = LCD 20x04

nets:
  VSS: LCM1602_IIC2.VSS, LCD3.VSS
  VDD: LCM1602_IIC2.VDD, LCD3.VDD
  N1: LCM1602_IIC2.V0, LCD3.V0
  N2: LCM1602_IIC2.RS, LCD3.RS
  N3: LCM1602_IIC2.RW, LCD3.R/W
  N4: LCM1602_IIC2.E, LCD3.E
  N5: LCM1602_IIC2.D0, LCD3.DB0
  N6: LCM1602_IIC2.D1, LCD3.DB1
  N7: LCM1602_IIC2.D2, LCD3.DB2
  N8: LCM1602_IIC2.D3, LCD3.DB3
  N9: LCM1602_IIC2.D4, LCD3.DB4
  N10: LCM1602_IIC2.D5, LCD3.DB5
  N11: LCM1602_IIC2.D6, LCD3.DB6
  N12: LCM1602_IIC2.D7, LCD3.DB7
  N13: LCM1602_IIC2.A, LCD3.LED+
  N14: LCM1602_IIC2.K, LCD3.LED-
  N15: LCM1602_IIC2.LED_A, LCM1602_IIC2.LED_B

custom parts:
  LCM1602 IIC: I2C-Module to use a 1602 or 2004 LCD on with the wire.h libory Serial LCD Modul
  LCD 20x04: LCD character display, 20 characters by 4 rows. Green.
